# Fritzing sketch arduino_bobbycar_step12 (saved by Fritzing 0.9.3b)
breadboards: 1

parts:
  Part1 = Arduino Uno (Rev3)
  hc-sr1 = hc-sr04
  LED1 = LED - 5mm [color="Red (633nm)" package="5 mm [THT]"]
  R1 = Resistor [tolerance=±5% resistance=220 package=THT]
  LED2 = LED - 5mm [color="Yellow (592nm)" package="5 mm [THT]"]
  LED3 = LED - 5mm [color="Green (565nm)" package="5 mm [THT]"]
  R2 = Resistor [tolerance=±5% resistance=220 package=THT]
  R3 = Resistor [tolerance=±5% resistance=220 package=THT]
  S1 = Pushbutton [package="[SMD]"]
  R4 = Rotary Potentiometer (Large) [maximum_resistance=100kΩ package=THT]
  U1 = LCD-16X2 [package=lcd-16x2]
  LCM1602_IIC1 = LCM1602 IIC [part_number="LCM1602 IIC" chip_label="LCM1602 IIC" package="DIP (Dual Inline) [THT]"]
  Piezo_buzzer4 = Piezo Buzzer  # not connected

nets:
  N1: Part1.A1, R4.wiper
  N2: Part1.A4/SDA, LCM1602_IIC1.SDA
  N3: Part1.A5/SCL, LCM1602_IIC1.SCL
  N4: Part1.D9_PWM, LED1.anode
  N5: Part1.D10_PWM/SS, hc-sr1.Echo
  N6: Part1.D11_PWM/MOSI, hc-sr1.Trig
  N7: Part1.D2, S1.Pin_3, S1.Pin_4
  N8: Part1.D5_PWM, LED3.anode
  N9: Part1.D6_PWM, LED2.anode
  VCC: Part1.5V, hc-sr1.VCC, R4.leg2, LCM1602_IIC1.VCC
  GND: hc-sr1.GND, R1.Pin_1, R2.Pin_1, R3.Pin_1, S1.Pin_1, S1.Pin_2, R4.leg1, LCM1602_IIC1.GND
  N10: LED1.cathode, R1.Pin_0
  N11: LED2.cathode, R2.Pin_0
  N12: LED3.cathode, R3.Pin_0
  VSS: U1.VSS, LCM1602_IIC1.VSS
  VDD: U1.VDD, LCM1602_IIC1.VDD
  N13: U1.VO, LCM1602_IIC1.V0
  N14: U1.RS, LCM1602_IIC1.RS
  N15: U1.R_W, LCM1602_IIC1.RW
  N16: U1.E, LCM1602_IIC1.E
  N17: U1.DB0, LCM1602_IIC1.D0
  N18: U1.DB1, LCM1602_IIC1.D1
  N19: U1.DB2, LCM1602_IIC1.D2
  N20: U1.DB3, LCM1602_IIC1.D3
  N21: U1.DB4, LCM1602_IIC1.D4
  N22: U1.DB5, LCM1602_IIC1.D5
  N23: U1.DB6, LCM1602_IIC1.D6
  N24: U1.DB7, LCM1602_IIC1.D7
  N25: U1.A, LCM1602_IIC1.A
  N26: U1.K, LCM1602_IIC1.K

custom parts:
  LCM1602 IIC: I2C-Module to use a 1602 or 2004 LCD on with the wire.h libory Serial LCD Modul
  Piezo Buzzer: Piezo buzzer PS1420P02CT
