# Fritzing sketch arduino_bobbycar_step9 (saved by Fritzing 0.9.3b)
breadboards: 1

parts:
  Part1 = Arduino Uno (Rev3)
  hc-sr1 = hc-sr04
  LED1 = LED - 5mm [color="Red (633nm)" package="5 mm [THT]"]
  R1 = Resistor [tolerance=±5% resistance=220 package=THT]
  LED2 = LED - 5mm [color="Yellow (592nm)" package="5 mm [THT]"]
  LED3 = LED - 5mm [color="Green (565nm)" package="5 mm [THT]"]
  R2 = Resistor [tolerance=±5% resistance=220 package=THT]
  R3 = Resistor [tolerance=±5% resistance=220 package=THT]
  Piezo_buzzer1 = Piezo Buzzer  # not connected

nets:
  N1: Part1.D9_PWM, LED1.anode
  N2: Part1.D10_PWM/SS, hc-sr1.Echo
  N3: Part1.D11_PWM/MOSI, hc-sr1.Trig
  N4: Part1.D5_PWM, LED3.anode
  N5: Part1.D6_PWM, LED2.anode
  5V: Part1.5V, hc-sr1.VCC
  N6: hc-sr1.GND, R1.Pin_1, R2.Pin_1, R3.Pin_1
  N7: LED1.cathode, R1.Pin_0
  N8: LED2.cathode, R2.Pin_0
  N9: LED3.cathode, R3.Pin_0

custom parts:
  Piezo Buzzer: Piezo buzzer PS1420P02CT
